# Fritzing sketch Untitled Sketch (saved by Fritzing 1.0.5)
breadboards: 1

parts:
  U1 = ESP32-38PinWide [part_number=ESP32-38PinWide]
  M3 = IR break beam 3mm tx [package=THT]
  M4 = IR break beam 3mm tx [package=THT]
  M5 = IR break beam 3mm rx [package=THT]
  M6 = IR break beam 3mm rx [package=THT]

nets:
  N1: U1.GPIO25, M6.pin2
  N2: U1.GPIO14, M5.pin2
  N3: U1.GND, M3.pin2, M4.pin2, M5.pin3, M6.pin3
  N4: U1.VIN, M3.pin1, M4.pin1, M5.pin1, M6.pin1

custom parts:
  ESP32-38PinWide: Generic 38-Pin ESP32 with wide format (only access to one side of pins on a breadboard) based on Stephen Lilley's HiLetgo ESP-WROOM-32 ESP32 ESP-32S Development Board.
  IR break beam 3mm tx: Infrared break beam Sensor tx module.
  IR break beam 3mm rx: Infrared break beam Sensor rx module.
