# Fritzing sketch Untitled Sketch1 (saved by Fritzing 1.0.5)
breadboards: 1

parts:
  M1 = IR break beam 3mm rx [package=THT]
  M2 = IR break beam 3mm tx [package=THT]
  U1 = ESP32-38PinWide [part_number=ESP32-38PinWide]
  M3 = IR break beam 3mm tx [package=THT]
  M4 = IR break beam 3mm rx [package=THT]

nets:
  N1: M1.pin1, M2.pin1, U1.VIN, M3.pin1, M4.pin1
  N2: M1.pin2, U1.GPIO14
  N3: M1.pin3, M2.pin2, U1.GPIO11, M3.pin2, M4.pin3
  N4: U1.GPIO25, M4.pin2

custom parts:
  IR break beam 3mm rx: Infrared break beam Sensor rx module.
  IR break beam 3mm tx: Infrared break beam Sensor tx module.
  ESP32-38PinWide: Generic 38-Pin ESP32 with wide format (only access to one side of pins on a breadboard) based on Stephen Lilley's HiLetgo ESP-WROOM-32 ESP32 ESP-32S Development Board.
